// Logisim project BeEight.circ as structural Verilog: 4 circuits, main circuit main
module main (
  input  RESET,
  input  HLT,
  input  RES,
  output [11:0] Address
);

  wire ALUD0, ALUD1, ALUD2, ALUD3, ALUD4, ALUD5, ALUD6, ALUD7, and_1_out, and_2_out, and_3_out, and_4_out,
       and_5_out, and_6_out, and_7_out, and_9_out, and_10_out, and_11_out, and_12_out, and_13_out,
       and_15_out, and_16_out, and_17_out, and_18_out, and_21_out, and_22_out, Carry, CLK, CLKIN, Cond0,
       Cond1, Cond2, ConditionalFlag, ConditionalResult, controlled_buffer_8_out, controlled_buffer_10_out,
       controlled_buffer_13_out, controlled_buffer_15_out, controlled_buffer_16_out,
       controlled_buffer_17_out, dbUpper, Equal, GreaterThan, ia, ialu, IdxCarry, iidx, im, inone, Inst0,
       Inst1, Inst2, Inst3, Inst4, inx, ipb, ipc, ipcs, isb, LessThan, M0, n74138_1_pin4, n74138_1_pin5,
       n74138_1_pin6, n74138_1_pin11, n74138_2_pin4, n74138_2_pin5, n74138_2_pin6, n74138_2_pin11,
       n74138_3_pin4, n74138_3_pin5, n74138_3_pin6, n74138_3_pin11, n74138_3_pin12, n74138_3_pin13,
       n74138_3_pin14, n74138_3_pin15, n74161_1_pin7, n74161_1_pin10, n74161_1_pin15, n74161_2_pin7,
       n74161_2_pin15, n74161_3_pin7, n74161_4_pin7, n74161_4_pin10, n74161_4_pin15, n74161_5_pin7,
       n74161_5_pin15, n74161_6_pin7, n74161_7_pin7, n74161_7_pin9, n74161_7_pin10, nor_1_out, not_1_out,
       not_2_out, not_3_out, not_4_out, not_5_out, not_6_out, not_7_out, not_8_out, not_9_out, not_10_out,
       not_12_out, not_13_out, not_14_out, not_15_out, not_16_out, not_17_out, not_18_out, not_19_out,
       not_20_out, not_21_out, not_22_out, not_23_out, not_24_out, not_25_out, not_26_out, not_27_out,
       not_28_out, not_29_out, not_30_out, not_31_out, not_32_out, not_33_out, not_34_out, not_35_out,
       not_36_out, not_37_out, not_38_out, not_39_out, not_40_out, not_41_out, not_42_out, not_43_out,
       not_44_out, not_45_out, not_46_out, not_47_out, not_48_out, nxt, oa, oalu, oidx, om, onone, opb, opc,
       opcs, or_2_out, or_4_out, or_5_out, or_6_out, or_7_out, or_8_out, or_10_out, or_15_out, or_16_out,
       osb, outspecial, PB4, PB5, PB6, PB7, pull_resistor_1_node, pull_resistor_2_node, pull_resistor_3_node,
       pull_resistor_4_node, pull_resistor_7_node, RESET_t, s_r_ff_1_qn, special, ucf;
  wire [2:0] pull_resistor_5_node;
  wire [3:0] DatabusUpper, InstructionCounter, pull_resistor_6_node;
  wire [6:0] rom_1_data;
  wire [7:0] Accumulator, adder_1_out, ALU, controlled_inverter_1_out, Databus, nand_1_out, PrimaryBuffer,
       SecondaryBuffer;
  wire [7:4] ProgramCounterStorageHigher_q;
  wire [11:0] Index, StoredAddress;

  not not_1 (not_1_out, special);
  or or_1 (dbUpper, not_1_out, im);
  or or_2 (or_2_out, opcs, special);
  not not_2 (not_2_out, iidx);
  OctalDTypeLatchOE ProgramCounterStorageLower (
    .D0(Databus[0]), .D1(Databus[1]), .D2(Databus[2]), .D3(Databus[3]), .D4(Databus[4]), .D5(Databus[5]),
    .D6(Databus[6]), .CK(and_1_out), .nOE(or_2_out), .D7(Databus[7]), .Q0(Databus[0]), .Q1(Databus[1]),
    .Q2(Databus[2]), .Q3(Databus[3]), .Q4(Databus[4]), .Q5(Databus[5]), .Q6(Databus[6]), .Q7(Databus[7]),
    .Q(StoredAddress[7:0]));
  and and_1 (and_1_out, CLK, not_3_out);
  OctalDTypeLatchOE ProgramCounterStorageHigher (
    .D0(DatabusUpper[0]), .D1(DatabusUpper[1]), .D2(DatabusUpper[2]), .D3(DatabusUpper[3]),
    .D4(pull_resistor_4_node), .D5(pull_resistor_3_node), .D6(pull_resistor_2_node), .CK(and_2_out),
    .nOE(or_2_out), .D7(pull_resistor_1_node), .Q0(DatabusUpper[0]), .Q1(DatabusUpper[1]),
    .Q2(DatabusUpper[2]), .Q3(DatabusUpper[3]), .Q({ProgramCounterStorageHigher_q, StoredAddress[11:8]}));  // open: Q4, Q5, Q6, Q7
  Pull_Resistor pull_resistor_1 (.node(pull_resistor_1_node));
  Pull_Resistor pull_resistor_2 (.node(pull_resistor_2_node));
  Pull_Resistor pull_resistor_3 (.node(pull_resistor_3_node));
  Pull_Resistor pull_resistor_4 (.node(pull_resistor_4_node));
  and and_2 (and_2_out, CLK, not_4_out);
  and and_3 (and_3_out, CLK, not_2_out);
  not not_3 (not_3_out, ipcs);
  not not_4 (not_4_out, ipcs);
  Hex_Digit_Display #(.decimalPoint("false")) hex_digit_display_1 (.value(Index[11:8]));
  _74161 #(.ShowInternalStructure("true")) u_74161_1 (
    .pin1(RESET_t), .pin2(and_3_out), .pin3(Databus[0]), .pin4(Databus[1]), .pin5(Databus[2]),
    .pin6(Databus[3]), .pin7(n74161_1_pin7), .pin15(n74161_1_pin15), .pin14(Index[0]), .pin13(Index[1]),
    .pin12(Index[2]), .pin11(Index[3]), .pin10(n74161_1_pin10), .pin9(inx));
  _74161 #(.ShowInternalStructure("true")) u_74161_2 (
    .pin1(RESET_t), .pin2(and_3_out), .pin3(Databus[4]), .pin4(Databus[5]), .pin5(Databus[6]),
    .pin6(Databus[7]), .pin7(n74161_2_pin7), .pin15(n74161_2_pin15), .pin14(Index[4]), .pin13(Index[5]),
    .pin12(Index[6]), .pin11(Index[7]), .pin10(n74161_1_pin15), .pin9(inx));
  _74161 #(.ShowInternalStructure("true")) u_74161_3 (
    .pin1(RESET_t), .pin2(and_3_out), .pin3(DatabusUpper[0]), .pin4(DatabusUpper[1]), .pin5(DatabusUpper[2]),
    .pin6(DatabusUpper[3]), .pin7(n74161_3_pin7), .pin15(IdxCarry), .pin14(Index[8]), .pin13(Index[9]),
    .pin12(Index[10]), .pin11(Index[11]), .pin10(n74161_2_pin15), .pin9(inx));
  Hex_Digit_Display #(.decimalPoint("false")) hex_digit_display_2 (.value(Index[7:4]));
  Hex_Digit_Display #(.decimalPoint("false")) hex_digit_display_3 (.value(Index[3:0]));
  Hex_Digit_Display #(.decimalPoint("false")) hex_digit_display_4 (.value({pull_resistor_5_node, Inst4}));
  Hex_Digit_Display #(.decimalPoint("false")) hex_digit_display_5 (.value({Inst3, Inst2, Inst1, Inst0}));
  Pull_Resistor pull_resistor_5 (.node(pull_resistor_5_node));
  Hex_Digit_Display #(.decimalPoint("false")) hex_digit_display_6 (.value(Address[11:8]));
  Hex_Digit_Display #(.decimalPoint("false")) hex_digit_display_7 (.value(Address[7:4]));
  Hex_Digit_Display #(.decimalPoint("false")) hex_digit_display_8 (.value(InstructionCounter));
  Hex_Digit_Display #(.decimalPoint("false")) hex_digit_display_9 (.value(Address[3:0]));
  Hex_Digit_Display #(.decimalPoint("false")) hex_digit_display_10 (.value(DatabusUpper));
  Hex_Digit_Display #(.decimalPoint("false")) hex_digit_display_11 (.value(Databus[7:4]));
  not not_5 (not_5_out, im);
  and and_4 (and_4_out, not_5_out, CLK);
  or or_3 (inx, iidx, not_6_out);
  not not_6 (not_6_out, oidx);
  assign Databus = not_9_out ? Index[7:0] : 8'bz;  // Controlled_Buffer controlled_buffer_1
  assign Databus = not_10_out ? {pull_resistor_6_node, Index[11:8]} : 8'bz;  // Controlled_Buffer controlled_buffer_2
  assign DatabusUpper = not_7_out ? Index[11:8] : 4'bz;  // Controlled_Buffer controlled_buffer_3
  Pull_Resistor pull_resistor_6 (.node(pull_resistor_6_node));
  not not_7 (not_7_out, oidx);
  Hex_Digit_Display #(.decimalPoint("false")) hex_digit_display_12 (.value(Accumulator[3:0]));
  Hex_Digit_Display #(.decimalPoint("false")) hex_digit_display_13 (.value(Accumulator[7:4]));
  Hex_Digit_Display #(.decimalPoint("false")) hex_digit_display_14 (.value(PrimaryBuffer[7:4]));
  Hex_Digit_Display #(.decimalPoint("false")) hex_digit_display_15 (.value(Databus[3:0]));
  RAM #(.addrWidth(12), .databus("bidir"), .trigger("high"), .\type ("nonvolatile")) ram_1 (
    .addr(Address), .we(and_4_out), .oe(not_8_out), .data(Databus));
  not not_8 (not_8_out, om);
  not not_9 (not_9_out, or_4_out);
  not not_10 (not_10_out, or_5_out);
  Hex_Digit_Display #(.decimalPoint("false")) hex_digit_display_16 (.value(ALU[7:4]));
  Hex_Digit_Display #(.decimalPoint("false")) hex_digit_display_17 (.value(ALU[3:0]));
  Hex_Digit_Display #(.decimalPoint("false")) hex_digit_display_18 (.value(PrimaryBuffer[3:0]));
  Hex_Digit_Display #(.decimalPoint("false")) hex_digit_display_19 (.value(SecondaryBuffer[7:4]));
  not not_11 (RESET_t, RESET);
  Clock u_CLK (.out(CLKIN));
  or or_4 (or_4_out, oidx, not_12_out);
  not not_12 (not_12_out, dbUpper);
  or or_5 (or_5_out, dbUpper, oidx);
  LED led_1 (.in(onone));
  LED led_2 (.in(om));
  LED led_3 (.in(inone));
  LED led_4 (.in(im));
  Hex_Digit_Display #(.decimalPoint("false")) hex_digit_display_20 (.value(SecondaryBuffer[3:0]));
  LED led_5 (.in(opb));
  LED led_6 (.in(osb));
  LED led_7 (.in(ipb));
  LED led_8 (.in(isb));
  Hex_Digit_Display #(.decimalPoint("false")) hex_digit_display_21 (.value(StoredAddress[11:8]));
  Hex_Digit_Display #(.decimalPoint("false")) hex_digit_display_22 (.value(StoredAddress[7:4]));
  not not_13 (not_13_out, osb);
  LED led_9 (.in(oa));
  LED led_10 (.in(oalu));
  LED led_11 (.in(ia));
  LED led_12 (.in(ialu));
  LED led_13 (.in(special));
  LED led_14 (.in(ConditionalFlag));
  Hex_Digit_Display #(.decimalPoint("false")) hex_digit_display_23 (.value(StoredAddress[3:0]));
  and and_5 (and_5_out, not_13_out, Inst0, Inst1, Inst2);
  not not_14 (not_14_out, special);
  assign {PB7, PB6, PB5, PB4} = special ? {Inst3, Inst2, Inst1, Inst0} : 4'bz;  // Controlled_Buffer controlled_buffer_4
  LED led_15 (.in(opc));
  LED led_16 (.in(opcs));
  LED led_17 (.in(ipc));
  LED led_18 (.in(ipcs));
  LED led_19 (.in(M0));
  LED led_20 (.in(nxt));
  LED RD (.in(om));
  LED WR (.in(im));
  not not_15 (not_15_out, and_5_out);
  and and_6 (and_6_out, and_5_out, ConditionalFlag);
  assign {PB7, PB6, PB5, PB4} = not_14_out ? Databus[7:4] : 4'bz;  // Controlled_Buffer controlled_buffer_5
  LED led_21 (.in(oidx));
  LED led_22 (.in(iidx));
  LED led_23 (.in(CLK));
  or or_6 (or_6_out, not_15_out, and_6_out);
  not not_16 (not_16_out, ipc);
  and and_7 (and_7_out, CLK, or_6_out, not_16_out);
  not not_17 (not_17_out, osb);
  S_R_Flip_Flop s_r_ff_1 (.reset(RES), .Qn(s_r_ff_1_qn), .preset(HLT));  // open: S, R, clk, Q
  assign DatabusUpper = not_17_out ? {Inst4, Cond2, Cond1, Cond0} : 4'bz;  // Controlled_Buffer controlled_buffer_6
  and and_8 (CLK, s_r_ff_1_qn, CLKIN);
  _74161 #(.ShowInternalStructure("true")) u_74161_4 (
    .pin1(RESET_t), .pin2(and_7_out), .pin3(Databus[0]), .pin4(Databus[1]), .pin5(Databus[2]),
    .pin6(Databus[3]), .pin7(n74161_4_pin7), .pin15(n74161_4_pin15), .pin14(Address[0]), .pin13(Address[1]),
    .pin12(Address[2]), .pin11(Address[3]), .pin10(n74161_4_pin10), .pin9(special));
  _74161 #(.ShowInternalStructure("true")) u_74161_5 (
    .pin1(RESET_t), .pin2(and_7_out), .pin3(Databus[4]), .pin4(Databus[5]), .pin5(Databus[6]),
    .pin6(Databus[7]), .pin7(n74161_5_pin7), .pin15(n74161_5_pin15), .pin14(Address[4]), .pin13(Address[5]),
    .pin12(Address[6]), .pin11(Address[7]), .pin10(n74161_4_pin15), .pin9(special));
  _74161 #(.ShowInternalStructure("true")) u_74161_6 (
    .pin1(RESET_t), .pin2(and_7_out), .pin3(DatabusUpper[0]), .pin4(DatabusUpper[1]), .pin5(DatabusUpper[2]),
    .pin6(DatabusUpper[3]), .pin7(n74161_6_pin7), .pin14(Address[8]), .pin13(Address[9]),
    .pin12(Address[10]), .pin11(Address[11]), .pin10(n74161_5_pin15), .pin9(special));  // open: pin15
  OctalDTypeLatchOE u_PrimaryBuffer (
    .D0(Databus[0]), .D1(Databus[1]), .D2(Databus[2]), .D3(Databus[3]), .D4(PB4), .D5(PB5), .D6(PB6),
    .CK(and_9_out), .nOE(1'b0), .D7(PB7), .Q0(Cond0), .Q1(Cond1), .Q2(Cond2), .Q3(Inst4), .Q4(Inst0),
    .Q5(Inst1), .Q6(Inst2), .Q7(Inst3), .Q(PrimaryBuffer));
  and and_9 (and_9_out, CLK, not_18_out);
  OctalDTypeLatchOE u_SecondaryBuffer (
    .D0(Databus[0]), .D1(Databus[1]), .D2(Databus[2]), .D3(Databus[3]), .D4(Databus[4]), .D5(Databus[5]),
    .D6(Databus[6]), .CK(and_10_out), .nOE(osb), .D7(Databus[7]), .Q0(Databus[0]), .Q1(Databus[1]),
    .Q2(Databus[2]), .Q3(Databus[3]), .Q4(Databus[4]), .Q5(Databus[5]), .Q6(Databus[6]), .Q7(Databus[7]),
    .Q(SecondaryBuffer));
  and and_10 (and_10_out, CLK, not_19_out);
  not not_18 (not_18_out, ipb);
  not not_19 (not_19_out, isb);
  not not_20 (not_20_out, RESET_t);
  not not_21 (not_21_out, opc);
  or or_7 (or_7_out, not_20_out, nxt);
  not not_22 (not_22_out, or_7_out);
  not not_23 (not_23_out, CLK);
  assign {DatabusUpper, Databus} = not_21_out ? Address : 12'bz;  // Controlled_Buffer controlled_buffer_7
  assign controlled_buffer_8_out = not_24_out ? Carry : 1'bz;  // Controlled_Buffer controlled_buffer_8
  not not_24 (not_24_out, ucf);
  assign controlled_buffer_8_out = ucf ? ConditionalResult : 1'bz;  // Controlled_Buffer controlled_buffer_9
  assign controlled_buffer_10_out = not_25_out ? controlled_buffer_8_out : 1'bz;  // Controlled_Buffer controlled_buffer_10
  not not_25 (not_25_out, not_26_out);
  assign controlled_buffer_10_out = not_26_out ? IdxCarry : 1'bz;  // Controlled_Buffer controlled_buffer_11
  not not_26 (not_26_out, inx);
  not not_27 (not_27_out, ialu);
  or or_8 (or_8_out, not_27_out, not_28_out);
  not not_28 (not_28_out, inx);
  _74161 #(.ShowInternalStructure("true")) u_74161_7 (
    .pin1(not_22_out), .pin2(not_23_out), .pin7(n74161_7_pin7), .pin14(InstructionCounter[0]),
    .pin13(InstructionCounter[1]), .pin12(InstructionCounter[2]), .pin11(InstructionCounter[3]),
    .pin10(n74161_7_pin10), .pin9(n74161_7_pin9));  // open: pin3, pin4, pin5, pin6, pin15
  ROM #(.addrWidth(9)) rom_1 (
    .addr({Inst4, Inst3, Inst2, Inst1, Inst0, InstructionCounter}),
    .data({outspecial, rom_1_data[6:4], special, rom_1_data[2:0]}));
  Register #(.width(1)) register_1 (
    .D(controlled_buffer_10_out), .en(or_8_out), .clk(CLK), .Q(ConditionalFlag));  // open: clr
  or or_9 (M0, InstructionCounter[0], InstructionCounter[1], InstructionCounter[2], InstructionCounter[3]);
  or or_10 (or_10_out, oalu, special);
  OctalDTypeLatchOE ALUBuffer (
    .D0(ALUD0), .D1(ALUD1), .D2(ALUD2), .D3(ALUD3), .D4(ALUD4), .D5(ALUD5), .D6(ALUD6), .CK(and_12_out),
    .nOE(or_10_out), .D7(ALUD7), .Q0(Databus[0]), .Q1(Databus[1]), .Q2(Databus[2]), .Q3(Databus[3]),
    .Q4(Databus[4]), .Q5(Databus[5]), .Q6(Databus[6]), .Q7(Databus[7]), .Q(ALU));
  _74138 #(.ShowInternalStructure("true")) u_74138_1 (
    .pin1(rom_1_data[0]), .pin2(rom_1_data[1]), .pin3(rom_1_data[2]), .pin4(n74138_1_pin4),
    .pin5(n74138_1_pin5), .pin6(n74138_1_pin6), .pin7(ipcs), .pin15(inone), .pin14(im), .pin13(ipb),
    .pin12(isb), .pin11(n74138_1_pin11), .pin10(ialu), .pin9(ipc));
  _74138 #(.ShowInternalStructure("true")) u_74138_2 (
    .pin1(rom_1_data[4]), .pin2(rom_1_data[5]), .pin3(rom_1_data[6]), .pin4(n74138_2_pin4),
    .pin5(n74138_2_pin5), .pin6(n74138_2_pin6), .pin7(opcs), .pin15(onone), .pin14(om), .pin13(opb),
    .pin12(osb), .pin11(n74138_2_pin11), .pin10(oalu), .pin9(opc));
  not not_29 (not_29_out, inone);
  not not_30 (not_30_out, onone);
  OctalDTypeLatchOE u_Accumulator (
    .D0(Databus[0]), .D1(Databus[1]), .D2(Databus[2]), .D3(Databus[3]), .D4(Databus[4]), .D5(Databus[5]),
    .D6(Databus[6]), .CK(and_11_out), .nOE(1'b0), .D7(Databus[7]), .Q0(Accumulator[0]), .Q1(Accumulator[1]),
    .Q2(Accumulator[2]), .Q3(Accumulator[3]), .Q4(Accumulator[4]), .Q5(Accumulator[5]), .Q6(Accumulator[6]),
    .Q7(Accumulator[7]));  // open: Q
  and and_11 (and_11_out, CLK, not_33_out);
  and and_12 (and_12_out, CLK, not_31_out, not_32_out);
  not not_31 (not_31_out, special);
  not not_32 (not_32_out, ialu);
  and and_13 (and_13_out, not_29_out, special);
  and and_14 (nxt, and_13_out, and_15_out);
  and and_15 (and_15_out, outspecial, not_30_out);
  not not_33 (not_33_out, ia);
  not not_34 (not_34_out, special);
  not not_35 (not_35_out, outspecial);
  assign Databus = not_36_out ? Accumulator : 8'bz;  // Controlled_Buffer controlled_buffer_12
  not not_36 (not_36_out, oa);
  or or_11 (iidx, n74138_1_pin11, not_34_out);
  or or_12 (ia, special, n74138_1_pin11);
  or or_13 (oidx, n74138_2_pin11, not_35_out);
  or or_14 (oa, outspecial, n74138_2_pin11);
  not not_37 (not_37_out, ucf);
  _74138 #(.ShowInternalStructure("true")) u_74138_3 (
    .pin1(Cond1), .pin2(Cond2), .pin4(n74138_3_pin4), .pin5(n74138_3_pin5), .pin6(n74138_3_pin6),
    .pin15(n74138_3_pin15), .pin14(n74138_3_pin14), .pin13(n74138_3_pin13), .pin12(n74138_3_pin12),
    .pin11(n74138_3_pin11));  // open: pin3, pin7, pin10, pin9
  not not_38 (not_38_out, n74138_3_pin15);
  Pull_Resistor pull_resistor_7 (.node(pull_resistor_7_node));
  assign controlled_buffer_13_out = not_38_out ? pull_resistor_7_node : 1'bz;  // Controlled_Buffer controlled_buffer_13
  assign controlled_inverter_1_out = ucf ? ~Accumulator : 8'bz;  // Controlled_Inverter controlled_inverter_1
  or or_15 (or_15_out, ConditionalFlag, ucf);
  assign controlled_inverter_1_out = not_37_out ? Accumulator : 8'bz;  // Controlled_Buffer controlled_buffer_14
  not not_39 (not_39_out, n74138_3_pin14);
  assign controlled_buffer_15_out = not_39_out ? Equal : 1'bz;  // Controlled_Buffer controlled_buffer_15
  not not_40 (not_40_out, n74138_3_pin13);
  assign controlled_buffer_16_out = not_40_out ? LessThan : 1'bz;  // Controlled_Buffer controlled_buffer_16
  not not_41 (not_41_out, n74138_3_pin12);
  assign controlled_buffer_17_out = not_41_out ? GreaterThan : 1'bz;  // Controlled_Buffer controlled_buffer_17
  and and_16 (and_16_out, not_43_out, Cond0, Inst0);
  Adder adder_1 (.a(Databus), .b(controlled_inverter_1_out), .out(adder_1_out), .cin(or_15_out), .cout(Carry));
  assign nand_1_out = ~(Accumulator & Databus);  // NAND_Gate nand_1, 8 bits wide
  assign {ALUD7, ALUD6, ALUD5, ALUD4, ALUD3, ALUD2, ALUD1, ALUD0} = and_16_out ? {ConditionalFlag, Accumulator[7:1]} : 8'bz;  // Controlled_Buffer controlled_buffer_18
  nor nor_1 (nor_1_out, adder_1_out[0], adder_1_out[1], adder_1_out[2], adder_1_out[3], adder_1_out[4], adder_1_out[5], adder_1_out[6], adder_1_out[7]);
  not not_42 (not_42_out, nor_1_out);
  not not_43 (not_43_out, Inst3);
  not not_44 (not_44_out, Cond0);
  and and_17 (and_17_out, not_43_out, not_44_out, Inst0);
  and and_18 (and_18_out, Inst3, Inst0);
  assign {ALUD7, ALUD6, ALUD5, ALUD4, ALUD3, ALUD2, ALUD1, ALUD0} = and_18_out ? nand_1_out : 8'bz;  // Controlled_Buffer controlled_buffer_19
  assign {ALUD7, ALUD6, ALUD5, ALUD4, ALUD3, ALUD2, ALUD1, ALUD0} = and_17_out ? {Accumulator[6:0], ConditionalFlag} : 8'bz;  // Controlled_Buffer controlled_buffer_20
  Pull_Resistor pull_resistor_8 (.node(controlled_buffer_13_out));
  Pull_Resistor pull_resistor_9 (.node(controlled_buffer_15_out));
  Pull_Resistor pull_resistor_10 (.node(controlled_buffer_16_out));
  Pull_Resistor pull_resistor_11 (.node(controlled_buffer_17_out));
  and and_19 (Equal, nor_1_out, Carry);
  and and_20 (LessThan, Carry, not_42_out);
  nor nor_2 (GreaterThan, Equal, LessThan);
  not not_45 (not_45_out, Inst0);
  assign {ALUD7, ALUD6, ALUD5, ALUD4, ALUD3, ALUD2, ALUD1, ALUD0} = not_45_out ? adder_1_out : 8'bz;  // Controlled_Buffer controlled_buffer_21
  or or_16 (or_16_out, controlled_buffer_13_out, controlled_buffer_15_out, controlled_buffer_16_out, controlled_buffer_17_out);
  assign ConditionalResult = and_21_out ? or_16_out : 1'bz;  // Controlled_Buffer controlled_buffer_22
  and and_21 (and_21_out, ucf, not_47_out);
  and and_22 (and_22_out, ucf, Cond0);
  not not_46 (not_46_out, or_16_out);
  assign ConditionalResult = and_22_out ? not_46_out : 1'bz;  // Controlled_Buffer controlled_buffer_23
  Pull_Resistor pull_resistor_12 (.node(ConditionalResult));
  not not_47 (not_47_out, Cond0);
  not not_48 (not_48_out, ialu);
  and and_23 (ucf, not_48_out, special);
  // also tied to GND on the sheet: {n74138_1_pin4, n74138_1_pin5, n74138_2_pin4, n74138_2_pin5, n74138_3_pin4, n74138_3_pin5}
  // also tied to VCC on the sheet: {n74161_1_pin7, n74161_2_pin7, n74161_3_pin7, n74161_1_pin10, n74161_4_pin7, n74161_5_pin7, n74161_6_pin7, n74161_4_pin10, n74161_7_pin7, n74161_7_pin10, n74161_7_pin9, n74138_1_pin6, n74138_2_pin6, n74138_3_pin6}

  // Other names for the same wires on the sheet: DB0 = Databus[0]; Memory[7:0] = Databus; PB0 = Databus[0];
  //   DB1 = Databus[1]; PB1 = Databus[1]; DB2 = Databus[2]; PB2 = Databus[2]; DB3 = Databus[3]; PB3 = Databus[3];
  //   DB4 = Databus[4]; DB5 = Databus[5]; DB6 = Databus[6]; DB7 = Databus[7]; DB8 = DatabusUpper[0];
  //   DB9 = DatabusUpper[1]; DB10 = DatabusUpper[2]; DB11 = DatabusUpper[3];
  //   Instruction[4:0] = {Inst4, Inst3, Inst2, Inst1, Inst0}; AQ0 = Accumulator[0]; AQ1 = Accumulator[1];
  //   AQ2 = Accumulator[2]; AQ3 = Accumulator[3]; AQ4 = Accumulator[4]; AQ5 = Accumulator[5]; AQ6 = Accumulator[6];
  //   AQ7 = Accumulator[7]; ALUin[7:0] = {ALUD7, ALUD6, ALUD5, ALUD4, ALUD3, ALUD2, ALUD1, ALUD0};
  //   Condition[2:0] = {Cond2, Cond1, Cond0}; HALT = HLT

  // Notes on the sheet:
  //   Index
  //   Program Counter
  //   contents of rom_1 (hex, n*v repeats v):
  //   12 e 14 e 88 11*0 12 e cc 88 12*0 12 e 13 e 35 54 88 9*0 12 e 5 54 88 11*0 12 e 1d e 88 11*0 12 e 13
  //   e 67 36 1a e 13 3c 76 88 4*0 12 e 13 36 88 11*0 12 e 13 e 36 88 10*0 12 e 13 e 67 36 14 76 88 7*0 12
  //   e 13 e 67 36 41 76 88 7*0 12 e 13 e 67 36 13 35 54 76 88 5*0 12 e 13 e 13 35 54 88 8*0 12 e 13 e 67
  //   36 1a e 13 36 c9 e c1 76 88 0 12 e 13 e 67 36 1a e 13 36 79 e 71 76 88 0 12 e 13 36 1a e 13 36 88
  //   7*0 12 e 13 36 1a e 13 36 88 7*0 12 e 67 c6 14 76 88 9*0 12 e 67 c6 41 76 88 9*0 12 e 67 c6 13 35 54
  //   76 88 7*0 12 e 67 c6 13 35 54 76 88 7*0 12 e 67 c6 1d 76 88 9*0 12 e 13 e 67 36 1a e 13 3c 76 88 4*0
  //   12 e 13 36 88 11*0 12 e 13 e 36 88 10*0 12 e 13 e 67 36 14 76 88 7*0 12 e 13 e 67 36 41 76 88 7*0 12
  //   e 13 e 67 36 13 35 54 76 88 5*0 12 e 13 e 13 35 54 88 8*0 12 e 13 e 67 36 1a e 13 36 c9 e c1 76 88 0
  //   12 e 13 e 67 36 1a e 13 36 79 e 71 76 88 0 12 e 13 36 1a e 13 36 88 7*0 12 e 13 36 1a e 13 36 88
  //   SL
  //   SR
  //   This is basically a Multiplexer
endmodule

module OctalDTypeLatchOE (
  input  D0,
  input  D1,
  input  D2,
  input  D3,
  input  D4,
  input  D5,
  input  D6,
  input  D7,
  input  CK,
  input  nOE,
  output [7:0] Q,
  output Q0,
  output Q1,
  output Q2,
  output Q3,
  output Q4,
  output Q5,
  output Q6,
  output Q7
);

  wire d_ff_1_qn, d_ff_2_qn, d_ff_3_qn, d_ff_4_qn, d_ff_5_qn, d_ff_6_qn, d_ff_7_qn, d_ff_8_qn, not_1_out,
       not_2_out, not_3_out;

  D_Flip_Flop d_ff_1 (.D(D0), .clk(not_2_out), .Q(Q[0]), .Qn(d_ff_1_qn));  // open: preset, reset
  not not_1 (not_1_out, CK);
  not not_2 (not_2_out, not_1_out);
  not not_3 (not_3_out, nOE);
  D_Flip_Flop d_ff_2 (.D(D1), .clk(not_2_out), .Q(Q[1]), .Qn(d_ff_2_qn));  // open: preset, reset
  assign Q0 = not_3_out ? ~d_ff_1_qn : 1'bz;  // Controlled_Inverter controlled_inverter_1
  D_Flip_Flop d_ff_3 (.D(D2), .clk(not_2_out), .Q(Q[2]), .Qn(d_ff_3_qn));  // open: preset, reset
  assign Q1 = not_3_out ? ~d_ff_2_qn : 1'bz;  // Controlled_Inverter controlled_inverter_2
  D_Flip_Flop d_ff_4 (.D(D3), .clk(not_2_out), .Q(Q[3]), .Qn(d_ff_4_qn));  // open: preset, reset
  assign Q2 = not_3_out ? ~d_ff_3_qn : 1'bz;  // Controlled_Inverter controlled_inverter_3
  D_Flip_Flop d_ff_5 (.D(D4), .clk(not_2_out), .Q(Q[4]), .Qn(d_ff_5_qn));  // open: preset, reset
  assign Q3 = not_3_out ? ~d_ff_4_qn : 1'bz;  // Controlled_Inverter controlled_inverter_4
  D_Flip_Flop d_ff_6 (.D(D5), .clk(not_2_out), .Q(Q[5]), .Qn(d_ff_6_qn));  // open: preset, reset
  assign Q4 = not_3_out ? ~d_ff_5_qn : 1'bz;  // Controlled_Inverter controlled_inverter_5
  D_Flip_Flop d_ff_7 (.D(D6), .clk(not_2_out), .Q(Q[6]), .Qn(d_ff_7_qn));  // open: preset, reset
  assign Q5 = not_3_out ? ~d_ff_6_qn : 1'bz;  // Controlled_Inverter controlled_inverter_6
  D_Flip_Flop d_ff_8 (.D(D7), .clk(not_2_out), .Q(Q[7]), .Qn(d_ff_8_qn));  // open: preset, reset
  assign Q6 = not_3_out ? ~d_ff_7_qn : 1'bz;  // Controlled_Inverter controlled_inverter_7
  assign Q7 = not_3_out ? ~d_ff_8_qn : 1'bz;  // Controlled_Inverter controlled_inverter_8
endmodule

module extTest (
);

  main main_1 ();  // open: RESET, HLT, RES, Address
endmodule

module QuadBusBuffers (
  input  nG1,
  input  A1,
  input  nG2,
  input  A2,
  input  nG3,
  input  A3,
  input  nG4,
  input  A4,
  output Y1,
  output Y2,
  output Y3,
  output Y4
);

  wire not_1_out, not_2_out, not_3_out, not_4_out;

  not not_1 (not_1_out, nG1);
  assign Y1 = not_1_out ? A1 : 1'bz;  // Controlled_Buffer controlled_buffer_1
  not not_2 (not_2_out, nG2);
  assign Y2 = not_2_out ? A2 : 1'bz;  // Controlled_Buffer controlled_buffer_2
  not not_3 (not_3_out, nG3);
  assign Y3 = not_3_out ? A3 : 1'bz;  // Controlled_Buffer controlled_buffer_3
  not not_4 (not_4_out, nG4);
  assign Y4 = not_4_out ? A4 : 1'bz;  // Controlled_Buffer controlled_buffer_4
endmodule
