// Logisim project MultiReg.circ as structural Verilog: 1 circuit, main circuit multireg
module multireg (
  input  RESET,
  input  EN,
  input  [4:0] SEL,
  input  CLK,
  input  [7:0] DATA,
  output [7:0] out_6,
  output [7:0] out_7,
  output [7:0] out_8,
  output [7:0] out_9,
  output [7:0] out_10,
  output [7:0] out_11,
  output [7:0] out_12,
  output [7:0] out_13,
  output [7:0] out_14,
  output [7:0] out_15,
  output [7:0] out_16,
  output [7:0] out_17,
  output [7:0] out_18,
  output [7:0] out_19,
  output [7:0] out_20,
  output [7:0] out_21,
  output [7:0] out_22,
  output [7:0] out_23,
  output [7:0] out_24,
  output [7:0] out_25,
  output [7:0] out_26,
  output [7:0] out_27,
  output [7:0] out_28,
  output [7:0] out_29,
  output [7:0] out_30,
  output [7:0] out_31,
  output [7:0] out_32,
  output [7:0] out_33,
  output [7:0] out_34,
  output [7:0] out_35,
  output [7:0] out_36,
  output [7:0] out_37,
  output [7:0] out_38
);

  wire demultiplexer_1_out0, demultiplexer_1_out1, demultiplexer_1_out2, demultiplexer_1_out3,
       demultiplexer_1_out4, demultiplexer_1_out5, demultiplexer_1_out6, demultiplexer_1_out7,
       demultiplexer_1_out8, demultiplexer_1_out9, demultiplexer_1_out10, demultiplexer_1_out11,
       demultiplexer_1_out12, demultiplexer_1_out13, demultiplexer_1_out14, demultiplexer_1_out15,
       demultiplexer_1_out16, demultiplexer_1_out17, demultiplexer_1_out18, demultiplexer_1_out19,
       demultiplexer_1_out20, demultiplexer_1_out21, demultiplexer_1_out22, demultiplexer_1_out23,
       demultiplexer_1_out24, demultiplexer_1_out25, demultiplexer_1_out26, demultiplexer_1_out27,
       demultiplexer_1_out28, demultiplexer_1_out29, demultiplexer_1_out30, demultiplexer_1_out31;

  Demultiplexer #(.select(5)) demultiplexer_1 (
    .out0(demultiplexer_1_out0), .out1(demultiplexer_1_out1), .out2(demultiplexer_1_out2),
    .out3(demultiplexer_1_out3), .out4(demultiplexer_1_out4), .out5(demultiplexer_1_out5),
    .out6(demultiplexer_1_out6), .out7(demultiplexer_1_out7), .out8(demultiplexer_1_out8),
    .out9(demultiplexer_1_out9), .out10(demultiplexer_1_out10), .out11(demultiplexer_1_out11),
    .out12(demultiplexer_1_out12), .out13(demultiplexer_1_out13), .out14(demultiplexer_1_out14),
    .out15(demultiplexer_1_out15), .out16(demultiplexer_1_out16), .out17(demultiplexer_1_out17),
    .out18(demultiplexer_1_out18), .out19(demultiplexer_1_out19), .out20(demultiplexer_1_out20),
    .out21(demultiplexer_1_out21), .out22(demultiplexer_1_out22), .out23(demultiplexer_1_out23),
    .out24(demultiplexer_1_out24), .out25(demultiplexer_1_out25), .out26(demultiplexer_1_out26),
    .out27(demultiplexer_1_out27), .out28(demultiplexer_1_out28), .out29(demultiplexer_1_out29),
    .out30(demultiplexer_1_out30), .out31(demultiplexer_1_out31), .in(EN), .sel(SEL));
  Register register_1 (.D(DATA), .en(demultiplexer_1_out0), .clk(CLK), .Q(out_6), .clr(RESET));
  Register register_2 (.D(DATA), .en(demultiplexer_1_out1), .clk(CLK), .Q(out_7), .clr(RESET));
  Register register_3 (.D(DATA), .clk(CLK), .Q(out_8), .clr(RESET));  // open: en
  Register register_4 (.D(DATA), .en(demultiplexer_1_out2), .clk(CLK), .Q(out_9), .clr(RESET));
  Register register_5 (.D(DATA), .en(demultiplexer_1_out3), .clk(CLK), .Q(out_10), .clr(RESET));
  Register register_6 (.D(DATA), .en(demultiplexer_1_out4), .clk(CLK), .Q(out_11), .clr(RESET));
  Register register_7 (.D(DATA), .en(demultiplexer_1_out5), .clk(CLK), .Q(out_12), .clr(RESET));
  Register register_8 (.D(DATA), .en(demultiplexer_1_out6), .clk(CLK), .Q(out_13), .clr(RESET));
  Register register_9 (.D(DATA), .en(demultiplexer_1_out7), .clk(CLK), .Q(out_14), .clr(RESET));
  Register register_10 (.D(DATA), .en(demultiplexer_1_out8), .clk(CLK), .Q(out_15), .clr(RESET));
  Register register_11 (.D(DATA), .en(demultiplexer_1_out9), .clk(CLK), .Q(out_16), .clr(RESET));
  Register register_12 (.D(DATA), .en(demultiplexer_1_out10), .clk(CLK), .Q(out_17), .clr(RESET));
  Register register_13 (.D(DATA), .en(demultiplexer_1_out11), .clk(CLK), .Q(out_18), .clr(RESET));
  Register register_14 (.D(DATA), .en(demultiplexer_1_out12), .clk(CLK), .Q(out_19), .clr(RESET));
  Register register_15 (.D(DATA), .en(demultiplexer_1_out13), .clk(CLK), .Q(out_20), .clr(RESET));
  Register register_16 (.D(DATA), .en(demultiplexer_1_out14), .clk(CLK), .Q(out_21), .clr(RESET));
  Register register_17 (.D(DATA), .en(demultiplexer_1_out15), .clk(CLK), .Q(out_22), .clr(RESET));
  Register register_18 (.D(DATA), .en(demultiplexer_1_out16), .clk(CLK), .Q(out_23), .clr(RESET));
  Register register_19 (.D(DATA), .en(demultiplexer_1_out17), .clk(CLK), .Q(out_24), .clr(RESET));
  Register register_20 (.D(DATA), .en(demultiplexer_1_out18), .clk(CLK), .Q(out_25), .clr(RESET));
  Register register_21 (.D(DATA), .en(demultiplexer_1_out19), .clk(CLK), .Q(out_26), .clr(RESET));
  Register register_22 (.D(DATA), .en(demultiplexer_1_out20), .clk(CLK), .Q(out_27), .clr(RESET));
  Register register_23 (.D(DATA), .en(demultiplexer_1_out21), .clk(CLK), .Q(out_28), .clr(RESET));
  Register register_24 (.D(DATA), .en(demultiplexer_1_out22), .clk(CLK), .Q(out_29), .clr(RESET));
  Register register_25 (.D(DATA), .en(demultiplexer_1_out23), .clk(CLK), .Q(out_30), .clr(RESET));
  Register register_26 (.D(DATA), .en(demultiplexer_1_out24), .clk(CLK), .Q(out_31), .clr(RESET));
  Register register_27 (.D(DATA), .en(demultiplexer_1_out25), .clk(CLK), .Q(out_32), .clr(RESET));
  Register register_28 (.D(DATA), .en(demultiplexer_1_out26), .clk(CLK), .Q(out_33), .clr(RESET));
  Register register_29 (.D(DATA), .en(demultiplexer_1_out27), .clk(CLK), .Q(out_34), .clr(RESET));
  Register register_30 (.D(DATA), .en(demultiplexer_1_out28), .clk(CLK), .Q(out_35), .clr(RESET));
  Register register_31 (.D(DATA), .en(demultiplexer_1_out29), .clk(CLK), .Q(out_36), .clr(RESET));
  Register register_32 (.D(DATA), .en(demultiplexer_1_out30), .clk(CLK), .Q(out_37), .clr(RESET));
  Register register_33 (.D(DATA), .en(demultiplexer_1_out31), .clk(CLK), .Q(out_38), .clr(RESET));
endmodule
